# Fritzing sketch welding_controller (saved by Fritzing 0.9.4)

parts:
  Part1 = Arduino Nano (Rev3.0) (ICSP)
  Rotary_Encoder1 = IDUINO Rotary Encoder SE055
  GLCD_128x1 = 128 x 64 Graphic LCD
  S1 = Limit Switch [package="Breakout Board"]
  S2 = Limit Switch [package="Breakout Board"]
  JP2 = Header 4 [package=molex-1x4_lock]
  J1 = Screw terminal - 2 pins [package=THT]
  S3 = Round Pushbutton

nets:
  GND: Part1.GND, Rotary_Encoder1.GND, JP2.4, J1.pin2, S3.leg1
  N1: Part1.D2, S3.leg0
  N2: Part1.D3, JP2.3
  N3: Part1.D4, JP2.2
  N4: Part1.D5, JP2.1
  N5: Part1.D6, Rotary_Encoder1.SW
  N6: Part1.D7, Rotary_Encoder1.DT
  N7: Part1.D8, Rotary_Encoder1.CLK
  N8: Part1.D9, S1.V, S2.V
  N9: Part1.D10, GLCD_128x1.4_RS
  N10: Part1.D11/MOSI, GLCD_128x1.5_RW
  N11: Part1.D12/MISO, GLCD_128x1.17_RST
  VIN: Part1.VIN, Part1.5V, J1.pin1
  N12: Part1.D13/SCK, GLCD_128x1.6_E
  N13: GLCD_128x1.1_Gnd, GLCD_128x1.14_DB7, GLCD_128x1.20_BL-
  N14: GLCD_128x1.2_Vcc, GLCD_128x1.19_BL+
  N15: S1.S, S2.S

notes:
  LIMIT SWITCHES
  ROTARY ENCODER
  SWITCH
  POWER IN
  5 to 9V
  EMERGENCY STOP PUSHBUTTON
  TO DRIVER

custom parts:
  IDUINO Rotary Encoder SE055: https://www.conrad.com/p/iduino-rotary-encoder-1-pcs-se055-1485328
  Limit Switch: Generic limit switch commonly found on 3D printers. Typical lever microswitch mounted on a PCB board with a 3 pin JST XH connector.
